// Logisim project rgb_driver.circ as structural Verilog: 2 circuits, main circuit main
module main (
);

  wire button_1_out, clock_1_out, driver_1_done, driver_1_latch, driver_1_pause, driver_1_row_clr,
       driver_1_row_cnt, driver_1_strobe, nor_1_out, not_1_out, pull_resistor_2_node, pull_resistor_6_node;
  wire [1:0] ram_1_data_2;
  wire [7:0] counter_1_q;
  wire [11:0] controlled_buffer_1_out, register_1_q;
  wire [15:0] ram_1_data;
  wire [16:0] driver_1_addr;

  Clock clock_1 (.out(clock_1_out));
  LED led_1 (.in(driver_1_done));
  Button button_1 (.out(button_1_out));
  Pull_Resistor pull_resistor_1 (.node(button_1_out));
  Pull_Resistor pull_resistor_2 (.node(pull_resistor_2_node));
  LED led_2 (.in(driver_1_latch));
  LED led_3 (.in(driver_1_strobe));
  driver driver_1 (
    .ACT(ram_1_data_2), .CLK(clock_1_out), .RESET(button_1_out), .DONE(driver_1_done),
    .LOAD(pull_resistor_2_node), .PAUSE(driver_1_pause), .STROBE(driver_1_strobe), .LATCH(driver_1_latch),
    .PWM(4'b0010), .ROW_CLR(driver_1_row_clr), .ROW_CNT(driver_1_row_cnt), .ADDR(driver_1_addr));
  RAM #(.addrWidth(17), .dataWidth(16), .bus("asynch")) ram_1 (
    .addr(driver_1_addr), .data({ram_1_data[15:14], ram_1_data_2, ram_1_data[11:0]}));  // open: sel, ld, clr
  Pull_Resistor pull_resistor_3 (.node(driver_1_row_cnt));
  Pull_Resistor pull_resistor_4 (.node(driver_1_row_clr));
  Counter counter_1 (
    .count(driver_1_row_cnt), .Q(counter_1_q), .clk(clock_1_out), .clr(driver_1_row_clr));  // open: load, D, carry
  assign controlled_buffer_1_out = not_1_out ? register_1_q : 12'bz;  // Controlled_Buffer controlled_buffer_1
  Register #(.width(12)) register_1 (.D(ram_1_data[11:0]), .Q(register_1_q), .clk(clock_1_out));  // open: en, clr
  not not_1 (not_1_out, pull_resistor_2_node);
  // Probe on counter_1_q
  Pull_Resistor pull_resistor_5 (.node(driver_1_pause));
  nor nor_1 (nor_1_out, clock_1_out, driver_1_pause, pull_resistor_6_node);
  Shift_Register #(.length(32)) shift_register_1 (
    .in(controlled_buffer_1_out[0]), .clk(nor_1_out));  // open: shift, out, load, clr, d0, q0, d1, q1, d2, q2, d3, q3, d4, q4, d5, q5, d6, q6, d7, q7, d8, q8, d9, q9, d10, q10, d11, q11, d12, q12, d13, q13, d14, q14, d15, q15, d16, q16, d17, q17, d18, q18, d19, q19, d20, q20, d21, q21, d22, q22, d23, q23, d24, q24, d25, q25, d26, q26, d27, q27, d28, q28, d29, q29, d30, q30, d31, q31
  Shift_Register #(.length(32)) shift_register_2 (
    .in(controlled_buffer_1_out[1]), .clk(nor_1_out));  // open: shift, out, load, clr, d0, q0, d1, q1, d2, q2, d3, q3, d4, q4, d5, q5, d6, q6, d7, q7, d8, q8, d9, q9, d10, q10, d11, q11, d12, q12, d13, q13, d14, q14, d15, q15, d16, q16, d17, q17, d18, q18, d19, q19, d20, q20, d21, q21, d22, q22, d23, q23, d24, q24, d25, q25, d26, q26, d27, q27, d28, q28, d29, q29, d30, q30, d31, q31
  Shift_Register #(.length(32)) shift_register_3 (
    .in(controlled_buffer_1_out[2]), .clk(nor_1_out));  // open: shift, out, load, clr, d0, q0, d1, q1, d2, q2, d3, q3, d4, q4, d5, q5, d6, q6, d7, q7, d8, q8, d9, q9, d10, q10, d11, q11, d12, q12, d13, q13, d14, q14, d15, q15, d16, q16, d17, q17, d18, q18, d19, q19, d20, q20, d21, q21, d22, q22, d23, q23, d24, q24, d25, q25, d26, q26, d27, q27, d28, q28, d29, q29, d30, q30, d31, q31
  Shift_Register #(.length(32)) shift_register_4 (
    .in(controlled_buffer_1_out[3]), .clk(nor_1_out));  // open: shift, out, load, clr, d0, q0, d1, q1, d2, q2, d3, q3, d4, q4, d5, q5, d6, q6, d7, q7, d8, q8, d9, q9, d10, q10, d11, q11, d12, q12, d13, q13, d14, q14, d15, q15, d16, q16, d17, q17, d18, q18, d19, q19, d20, q20, d21, q21, d22, q22, d23, q23, d24, q24, d25, q25, d26, q26, d27, q27, d28, q28, d29, q29, d30, q30, d31, q31
  Pull_Resistor pull_resistor_6 (.node(pull_resistor_6_node));
endmodule

module driver (
  input  [1:0] ACT,
  input  CLK,
  input  RESET,
  input  LOAD,
  input  [3:0] PWM,
  output ROW_CLR,
  output ROW_CNT,
  output [16:0] ADDR,
  output DONE,
  output PAUSE,
  output STROBE,
  output LATCH
);

  wire and_2_out, and_3_out, and_5_out, and_6_out, and_7_out, and_8_out, and_9_out, and_10_out, and_11_out,
       and_12_out, and_13_out, and_14_out, and_15_out, comparator_1_eq, comparator_2_eq, d_ff_1_q, d_ff_2_q,
       d_ff_3_q, j_k_ff_1_q, j_k_ff_2_q, j_k_ff_2_qn, nand_1_out, not_1_out, not_2_out, or_2_out, or_3_out,
       or_4_out, or_5_out, or_6_out;
  wire [2:0] or_1_out, register_1_q;
  wire [3:0] counter_1_q;
  wire [15:0] counter_3_q, decoder_1_out0, decoder_2_out0;

  assign PAUSE = not_1_out ? and_5_out : 1'bz;  // Controlled_Buffer controlled_buffer_1
  assign STROBE = not_1_out ? and_2_out : 1'bz;  // Controlled_Buffer controlled_buffer_2
  assign LATCH = not_1_out ? and_3_out : 1'bz;  // Controlled_Buffer controlled_buffer_3
  and and_1 (DONE, register_1_q[2], and_15_out);
  not not_1 (not_1_out, LOAD);
  and and_2 (and_2_out, and_5_out, d_ff_3_q, j_k_ff_2_q, ~or_6_out);  // AND_Gate
  and and_3 (and_3_out, and_5_out, j_k_ff_2_qn);
  or or_1 (or_1_out[0], ACT[0], ACT[1]);
  and and_4 (or_1_out[2], ACT[1], ACT[0]);
  D_Flip_Flop d_ff_1 (.clk(CLK), .D(register_1_q[0]), .Q(d_ff_1_q), .reset(RESET));  // open: Qn, preset, en
  and and_5 (and_5_out, register_1_q[0], d_ff_1_q);
  assign ROW_CLR = not_1_out ? or_2_out : 1'bz;  // Controlled_Buffer controlled_buffer_4
  or or_2 (or_2_out, RESET, and_6_out);
  and and_6 (and_6_out, register_1_q[2], and_15_out);
  Register #(.width(3)) register_1 (
    .D({or_1_out[2], ACT[1], or_1_out[0]}), .Q(register_1_q), .clk(CLK), .clr(RESET));  // open: en
  not not_2 (not_2_out, and_5_out);
  assign ROW_CNT = not_1_out ? and_7_out : 1'bz;  // Controlled_Buffer controlled_buffer_5
  and and_7 (and_7_out, register_1_q[1], and_15_out);
  and and_8 (and_8_out, register_1_q[1], and_10_out);
  or or_3 (or_3_out, and_8_out, RESET);
  and and_9 (and_9_out, and_10_out, register_1_q[0], ~register_1_q[1]);  // AND_Gate
  and and_10 (and_10_out, and_15_out, ~d_ff_2_q);  // AND_Gate
  or or_4 (or_4_out, ~or_1_out[0], LOAD, and_11_out);  // OR_Gate
  and and_11 (and_11_out, ~register_1_q[2], and_15_out);  // AND_Gate
  or or_5 (or_5_out, not_2_out, j_k_ff_1_q, RESET, and_12_out);
  Counter #(.width(4), .max('hf)) counter_1 (
    .load(or_3_out), .D(PWM), .count(and_9_out), .Q(counter_1_q), .clk(CLK));  // open: carry, clr
  Counter #(.width(17), .max('h1ffff)) counter_2 (
    .count(or_4_out), .Q(ADDR), .clk(CLK), .clr(RESET));  // open: load, D, carry
  and and_12 (and_12_out, ~d_ff_3_q, j_k_ff_2_q);  // AND_Gate
  and and_13 (and_13_out, nand_1_out, and_5_out);
  Counter #(.width(16), .max('hffff)) counter_3 (
    .count(and_13_out), .Q(counter_3_q), .clk(CLK), .clr(or_5_out));  // open: load, D, carry
  Decoder #(.select(4)) decoder_1 (
    .out0(decoder_1_out0[0]), .out1(decoder_1_out0[1]), .out2(decoder_1_out0[2]), .out3(decoder_1_out0[3]),
    .out4(decoder_1_out0[4]), .out5(decoder_1_out0[5]), .out6(decoder_1_out0[6]), .out7(decoder_1_out0[7]),
    .out8(decoder_1_out0[8]), .out9(decoder_1_out0[9]), .out10(decoder_1_out0[10]),
    .out11(decoder_1_out0[11]), .out12(decoder_1_out0[12]), .out13(decoder_1_out0[13]),
    .out14(decoder_1_out0[14]), .out15(decoder_1_out0[15]), .sel(PWM));  // open: en
  Decoder #(.select(4)) decoder_2 (
    .out0(decoder_2_out0[0]), .out1(decoder_2_out0[1]), .out2(decoder_2_out0[2]), .out3(decoder_2_out0[3]),
    .out4(decoder_2_out0[4]), .out5(decoder_2_out0[5]), .out6(decoder_2_out0[6]), .out7(decoder_2_out0[7]),
    .out8(decoder_2_out0[8]), .out9(decoder_2_out0[9]), .out10(decoder_2_out0[10]),
    .out11(decoder_2_out0[11]), .out12(decoder_2_out0[12]), .out13(decoder_2_out0[13]),
    .out14(decoder_2_out0[14]), .out15(decoder_2_out0[15]), .sel(counter_1_q));  // open: en
  D_Flip_Flop d_ff_2 (.clk(CLK), .D(and_15_out), .Q(d_ff_2_q), .reset(RESET));  // open: Qn, preset, en
  nand nand_1 (nand_1_out, j_k_ff_2_q, j_k_ff_1_q);
  Comparator #(.width(16)) comparator_1 (.a(counter_3_q), .b(decoder_1_out0), .eq(comparator_1_eq));  // open: gt, lt
  or or_6 (or_6_out, j_k_ff_1_q, and_14_out);
  Comparator #(.width(16)) comparator_2 (.a(counter_3_q), .b(decoder_2_out0), .eq(comparator_2_eq));  // open: gt, lt
  and and_14 (and_14_out, comparator_2_eq, d_ff_3_q);
  J_K_Flip_Flop j_k_ff_1 (
    .J(and_14_out), .clk(CLK), .K(not_2_out), .Q(j_k_ff_1_q), .reset(RESET));  // open: Qn, preset, en
  J_K_Flip_Flop j_k_ff_2 (
    .J(comparator_1_eq), .clk(CLK), .K(not_2_out), .Q(j_k_ff_2_q), .Qn(j_k_ff_2_qn), .reset(RESET));  // open: preset, en
  D_Flip_Flop d_ff_3 (.clk(CLK), .D(j_k_ff_2_q), .Q(d_ff_3_q), .reset(RESET));  // open: Qn, preset, en
  and and_15 (and_15_out, j_k_ff_2_q, and_5_out, j_k_ff_1_q);
endmodule
